# Fritzing sketch blinkByLight (saved by Fritzing 0.9.2b)
breadboards: 1

parts:
  Parte1 = Arduino Uno (Rev3)
  R1 = Resistor [tolerance=±0.05% resistance=220 power=10k package=THT]
  R2 = Photocell (LDR) [package=THT]

nets:
  N1: Parte1.A0, R1.Pin_1, R2.pin_0
  N2: Parte1.5V, R2.pin_1
  N3: Parte1.GND, R1.Pin_0
